# Fritzing sketch OpiaPlan (saved by Fritzing 0.9.2b)
breadboards: 1

parts:
  Leonardo = Arduino Leonardo (Rev3b)
  R2 = Trimmer Potentiometer [maximum_resistance=10kΩ package=THT]  # not connected
  R2_2 = Trimmer Potentiometer [maximum_resistance=10kΩ package=THT]
  R1 = Trimmer Potentiometer [maximum_resistance=10kΩ package=THT]
  U1 = mystery part, 3 pins [chip_label="Hall Effect Sensor"]
  R3 = Resistor [tolerance=±5% resistance=10k package=THT]

nets:
  N1: Leonardo.D2/SDA, Leonardo.SDA, U1.pin3
  N2: Leonardo.A2, R1.leg2
  N3: Leonardo.A3, R2_2.leg2
  5V: R2_2.leg1, R1.leg1
  GND: R2_2.wiper, R1.wiper, U1.pin2, R3.Pin_1
  3.3V: U1.pin1, R3.Pin_0
